# Fritzing sketch Forcecast Sketch (saved by Fritzing 1.0.1rc)
breadboards: 1

parts:
  WeMos_D1_Mini1 = WeMos D1 Mini  # not connected
  S1 = Pushbutton [package="[SMD]"]
  U1 = LCD-16X2 [package=lcd-16x2_noholes]
  LCM1602_IIC1 = LCM1602 IIC [part_number="LCM1602 IIC" chip_label="LCM1602 IIC" package="DIP (Dual Inline) [THT]"]
  RHT1 = Humidity and Temperature Sensor RHT03
  R2 = Resistor [tolerance=±5% resistance=10k package="2010 [SMD]"]
  R1 = Resistor [tolerance=±5% resistance=10k package="2010 [SMD]"]
  Mod1 = KY-016
  R3 = Resistor [tolerance=±5% resistance=100 package="2010 [SMD]"]

nets:
  N1: S1.Pin_1, S1.Pin_2
  VCC: S1.Pin_3, S1.Pin_4, LCM1602_IIC1.VCC, RHT1.Vcc, R2.Pin_1
  VSS: U1.VSS, LCM1602_IIC1.VSS
  VDD: U1.VDD, LCM1602_IIC1.VDD
  N2: U1.VO, LCM1602_IIC1.V0
  N3: U1.RS, LCM1602_IIC1.RS
  N4: U1.R_W, LCM1602_IIC1.RW
  N5: U1.E, LCM1602_IIC1.E
  N6: U1.DB0, LCM1602_IIC1.D0
  N7: U1.DB1, LCM1602_IIC1.D1
  N8: U1.DB2, LCM1602_IIC1.D2
  N9: U1.DB3, LCM1602_IIC1.D3
  N10: U1.DB4, LCM1602_IIC1.D4
  N11: U1.DB5, LCM1602_IIC1.D5
  N12: U1.DB6, LCM1602_IIC1.D6
  N13: U1.DB7, LCM1602_IIC1.D7
  N14: U1.A, LCM1602_IIC1.A
  N15: U1.K, LCM1602_IIC1.K
  N16: LCM1602_IIC1.GND, RHT1.GND_2, R1.Pin_1, Mod1.connector4
  N17: RHT1.Data-signal, R2.Pin_0
  N18: Mod1.connector1, R3.Pin_0

custom parts:
  LCM1602 IIC: I2C-Module to use a 1602 or 2004 LCD on with the wire.h libory Serial LCD Modul
